# Fritzing sketch ESP8266-12 breakout board 2layer V2z1 (saved by Fritzing 0.9.3b)
circuit board: 4.99713cm x 3.1231cm
breadboards: 1

parts:
  RST = SWITCH-MOMENTARY-2 [package=tactile_switch_smd]
  PRG = SWITCH-MOMENTARY-2 [package=tactile_switch_smd]
  PRG2 = Solder Jumper [package=sj_2s-no]
  RST2 = Solder Jumper [package=sj_2s-no]
  WK = Solder Jumper [package=sj_2s-no]
  TTL1 = female pin header, 6 pins [form="♀ (female)"]
  ESP8267 = ESP8266 WiFi Module [part_number=ESP8266]
  R15 = Resistor [tolerance=±5% resistance=10k package="1206 [SMD]"]
  R16 = Resistor [tolerance=±5% resistance=10k package="1206 [SMD]"]
  R17 = Resistor [tolerance=±5% resistance=10k package="1206 [SMD]"]
  R18 = Resistor [tolerance=±5% resistance=10k package="1206 [SMD]"]
  R19 = Resistor [tolerance=±5% resistance=10k package="1206 [SMD]"]
  CON3 = male pin header, 8 pins [form="♂ (male)"]
  CON4 = male pin header, 8 pins [form="♂ (male)"]
  C2 = Electrolytic Capacitor [capacitance=0.22mF voltage=10V package="100 mil [THT, electrolytic]"]
  TTL3V3 = male pin header, 3 pins [form="♂ (male)"]
  R20 = Resistor [tolerance=±5% resistance=10m package="1206 [SMD]"]
  R21 = Resistor [tolerance=±5% resistance=2m package="1206 [SMD]"]
  DS1 = DS18B20 1-Wire Temperature Sensor [part_number=DS18B20]

nets:
  GND: RST.1, PRG.1, TTL1.pin1, ESP8267.GND, R15.Pin_0, CON3.pin8, C2.-, TTL3V3.pin2, R21.Pin_0, DS1.GND
  N1: RST.2, RST2.1, WK.1, ESP8267.REST, R16.Pin_0, CON4.pin1
  N2: PRG.2, PRG2.1, ESP8267.GPIO_0, R18.Pin_0, CON3.pin5
  N3: PRG2.2, TTL1.pin6
  N4: RST2.2, TTL1.pin2
  N5: WK.2, ESP8267.GPIO_16, CON4.pin4
  N6: TTL1.pin4, ESP8267.RXD, CON3.pin2
  N7: TTL1.pin5, ESP8267.TXD, CON3.pin1
  VCC: ESP8267.VCC, R16.Pin_1, R17.Pin_1, R18.Pin_1, R19.Pin_1, CON4.pin8, C2.+, TTL3V3.pin1, R20.Pin_1, DS1.VDD
  N8: ESP8267.GPIO_2, R17.Pin_0, CON3.pin6
  N9: ESP8267.CH_PD, R19.Pin_0, CON4.pin3
  N10: ESP8267.GPIO_15, R15.Pin_1, CON3.pin7
  N11: ESP8267.GPIO_4, CON3.pin3
  N12: ESP8267.GPIO_5, CON3.pin4
  N13: ESP8267.ADC_0, CON4.pin2, R20.Pin_0, R21.Pin_1
  N14: ESP8267.GPIO_14, CON4.pin5, DS1.DQ
  N15: ESP8267.GPIO_12, CON4.pin6
  N16: ESP8267.GPIO_13, CON4.pin7

custom parts:
  ESP8266 WiFi Module: Generic WiFi Module based on the ESP8266 with onboard PCB antenna and UART communications
